# Fritzing sketch dht11 (saved by Fritzing 0.9.10b)
breadboards: 1

parts:
  Mod1 = Raspberry Pi 4B
  RHT1 = Humidity and Temperature Sensor RHT03
  R1 = Resistor [tolerance=±5% power=0.25 resistance=220 package=THT]

nets:
  3V3: Mod1.3V3, RHT1.Vcc, R1.Pin_0
  N1: Mod1.GPIO17, RHT1.Data-signal, R1.Pin_1
  N2: Mod1.GND, RHT1.GND_1
